# Fritzing sketch weatherstation (saved by Fritzing 0.9.3b)
circuit board: 6.60402cm x 5.1378cm

parts:
  LCD = LCD screen
  BMP180 = Barometric Pressure Sensor - BMP180 Breakout (GY-68)
  DHT22 = DHT22 Humidity and Temperature Sensor
  LCM1602_IIC1 = LCM1602 IIC [part_number="LCM1602 IIC" chip_label="LCM1602 IIC" package="DIP (Dual Inline) [THT]"]
  NodeMCU = NodeMCU V1.0

nets:
  VSS: LCD.VSS, LCM1602_IIC1.VSS
  VDD: LCD.VDD, LCM1602_IIC1.VDD
  N1: LCD.V0, LCM1602_IIC1.V0
  N2: LCD.RS, LCM1602_IIC1.RS
  N3: LCD.R/W, LCM1602_IIC1.RW
  N4: LCD.E, LCM1602_IIC1.E
  N5: LCD.DB0, LCM1602_IIC1.D0
  N6: LCD.DB1, LCM1602_IIC1.D1
  N7: LCD.DB2, LCM1602_IIC1.D2
  N8: LCD.DB3, LCM1602_IIC1.D3
  N9: LCD.DB4, LCM1602_IIC1.D4
  N10: LCD.DB5, LCM1602_IIC1.D5
  N11: LCD.DB6, LCM1602_IIC1.D6
  N12: LCD.DB7, LCM1602_IIC1.D7
  N13: LCD.LED+, LCM1602_IIC1.A
  N14: LCD.LED-, LCM1602_IIC1.K
  VCC: BMP180.VCC, DHT22.VDD, NodeMCU.3V3
  GND: BMP180.GND, DHT22.GND, LCM1602_IIC1.GND, NodeMCU.GND
  N15: BMP180.SCL, NodeMCU.D1
  N16: BMP180.SDA, NodeMCU.D2
  N17: DHT22.DATA, NodeMCU.D5
  VCC_2: LCM1602_IIC1.VCC, NodeMCU.Vin
  N18: LCM1602_IIC1.SDA, NodeMCU.D7
  N19: LCM1602_IIC1.SCL, NodeMCU.D6

custom parts:
  LCM1602 IIC: I2C-Module to use a 1602 or 2004 LCD on with the wire.h libory Serial LCD Modul
  NodeMCU V1.0: ESP8266 based NodeMCU
